# Fritzing sketch CMPE 495 Hardware Design (saved by Fritzing 0.9.10b)

parts:
  M1 = Grove GSR Sensor
  Mod3 = AD8232 HeartRate Monitor [part_number=SEN-12650]
  Mod1 = Raspberry Pi 4B
  T2 = LM35 Temperature Sensor [package="TO92 [THT]"]
  Part1 = Adafruit ADS1115 16Bit I2C ADC [part_number="Adafruit #1085"]

nets:
  N1: M1.SIG, Part1.AIN2
  N2: Mod3.OUTPUT, Part1.AIN0
  3V3: Mod1.3V3, Part1.VDD
  N3: Mod1.GPIO2, Part1.SDA
  N4: Mod1.GPIO3, Part1.SCL
  GND: Mod1.GND, Part1.GND
  N5: T2.Vout, Part1.AIN1

custom parts:
  Grove GSR Sensor: GSR stands for galvanic skin response, is a method of measuring the electrical conductance of the skin. Strong emotion can cause stimulus to your sympathetic nervous system, resulting more sweat being secreted by the sweat glands.
  AD8232 HeartRate Monitor: Sparkfun single lead heart rate monitor - Ad8232.
  Adafruit ADS1115 16Bit I2C ADC: For microcontrollers without an analog-to-digital converter or when you want a higher-precision ADC, the ADS1115 provides 16-bit precision at 860 samples/second over I2C. The chip can be configured as 4 single-ended input channels, or two differential channels. As a nice bonus, it even includes a programmable gain amplifier, up to x16, to help boost up smaller single/differential signals to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
